# Fritzing sketch deskinator-wiring (saved by Fritzing 1.0.5)
breadboards: 3

parts:
  IMU = Adafruit BNO085 9-DOF Orientation IMU Fusion [part_number="Addfruit #4754"]
  NEMA17-1 = Stepper Motor - Bipolar
  NEMA17-2 = Stepper Motor - Bipolar
  RBPi = Raspberry Pi 4B
  Edge-Prox-0 = Adafruit APDS9960 Proximity Sensor [part_number="Adafruit #3595"]
  Lipo = 4S Li-ion/LiPo 14.8 V XT60 [package=lipo-2000]
  Vacuum-DC = DC Vacuum Fan 12V
  XL4015-5_1V = DC_DC_XL4015 [package=board_screw]
  Driver-1 = TMC2209 [package=THT]
  Driver-2 = TMC2209 [package=THT]
  EDGE-MUX = Adafruit TCA9548A
  Edge-Prox-1 = Adafruit APDS9960 Proximity Sensor [part_number="Adafruit #3595"]
  Edge-Prox-2 = Adafruit APDS9960 Proximity Sensor [part_number="Adafruit #3595"]
  Wave-Prox-0 = Adafruit APDS9960 Proximity Sensor [part_number="Adafruit #3595"]
  NPN-Trans = NPN-Transistor [package="TO92 [THT]"]
  10k-Res = 10kΩ Resistor [package="0402 [SMD]"]
  Buzzer = Piezo Speaker
  Edge-Prox-3 = Adafruit APDS9960 Proximity Sensor [part_number="Adafruit #3595"]

nets:
  GND: IMU.GND, RBPi.GND, Edge-Prox-0.GND, Lipo.-, Vacuum-DC.pin_2, XL4015-5_1V.IN-, XL4015-5_1V.OUT-, Driver-1.GND, Driver-2.GND, EDGE-MUX.GND, Edge-Prox-1.GND, Edge-Prox-2.GND, Wave-Prox-0.GND, NPN-Trans.E, Buzzer.pin1, Edge-Prox-3.GND
  VCC: IMU.VCC, RBPi.3V3, Edge-Prox-0.VCC, Driver-1.VIO, Driver-2.VIO, EDGE-MUX.VCC, Edge-Prox-1.VCC, Edge-Prox-2.VCC, Wave-Prox-0.VCC, Edge-Prox-3.VCC
  N1: IMU.SCL/SCK/RX, RBPi.GPIO14
  N2: IMU.SDA/MISO/TX, RBPi.GPIO15
  N3: NEMA17-1.A, Driver-1.M1B
  N4: NEMA17-1.C, Driver-1.M1A
  N5: NEMA17-1.B, Driver-1.M2A
  N6: NEMA17-1.D, Driver-1.M2B
  N7: NEMA17-2.A, Driver-2.M1B
  N8: NEMA17-2.C, Driver-2.M1A
  N9: NEMA17-2.B, Driver-2.M2A
  N10: NEMA17-2.D, Driver-2.M2B
  N11: RBPi.5V, XL4015-5_1V.OUT+
  N12: RBPi.GPIO2, EDGE-MUX.INPUTSDA
  N13: RBPi.GPIO3, EDGE-MUX.INPUTSCL
  N14: RBPi.GPIO4, Wave-Prox-0.SCL
  N15: RBPi.GPIO17, Wave-Prox-0.SDA
  N16: RBPi.GPIO22, Driver-2.Step
  N17: RBPi.GPIO23, Driver-2.Dir
  N18: RBPi.GPIO24, 10k-Res.Pin_1
  N19: RBPi.GPIO16, Driver-1.EN, Driver-2.EN
  N20: RBPi.GPIO20, Driver-1.Step
  N21: RBPi.GPIO21, Driver-1.Dir
  N22: Edge-Prox-0.SDA, EDGE-MUX.0SDA
  N23: Edge-Prox-0.SCL, EDGE-MUX.0SCL
  N24: Lipo.+, Vacuum-DC.pin_1, XL4015-5_1V.IN+, Driver-1.VM, Driver-2.VM
  N25: EDGE-MUX.2SDA, Edge-Prox-2.SDA
  N26: EDGE-MUX.2SCL, Edge-Prox-2.SCL
  N27: EDGE-MUX.3SDA, Edge-Prox-3.SDA
  N28: EDGE-MUX.3SCL, Edge-Prox-3.SCL
  N29: EDGE-MUX.1SDA, Edge-Prox-1.SDA
  N30: EDGE-MUX.1SCL, Edge-Prox-1.SCL
  N31: NPN-Trans.B, 10k-Res.Pin_0
  N32: NPN-Trans.C, Buzzer.pin2

notes:
  12V
  5.10V

custom parts:
  Adafruit APDS9960 Proximity Sensor: This breakout is chock full o' sensors! Add basic gesture sensing, RGB color sensing, proximity sensing, or ambient light sensing to your project with the Adafruit APDS9960 Proximity, Light, RGB and Gesture Sensor. When connected to your microcontroller (running our library code) it can detect simple gestures (left to right, right to left, up to down, down to up are currently supported),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
  4S Li-ion/LiPo 14.8 V XT60: 4S Li-ion/LiPo pack, 14.8 V nominal (16.8 V full), XT60 connector.
  DC Vacuum Fan 12V: DC Vacuum Fan
  DC_DC_XL4015: DC-DC Converter step down voltage regulator XL4016 custom sketch.
  TMC2209: TMC2209-LA stepper motor controller and driver. Supply voltage 4.75-28V Iphase up to 1.77A rms (2.5A peak)
  Adafruit TCA9548A: You just found the perfect I2C sensor, and you want to wire up two or three or more of them to your Arduino when you realize "Uh oh, this chip has a fixed I2C address, and from what I know about I2C, you cannot have two devices with the same address on the same SDA/SCL pins!" Are you out of luck? You would be, if you didn't have this ultra-cool TCA9548A 1-to-8 I2C multiplexer! Finally, a way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
  10kΩ Resistor: Resistor Basic schematic elements and footprints for 0603, 1206, and PTH resistors.
